# Fritzing sketch HDC1000_LCD5110_AVR_Thermo (saved by Fritzing 0.9.3b)
breadboards: 2

parts:
  U1 = mystery part, 8 pins [chip_label=Nokia5110]
  C1 = Ceramic Capacitor [capacitance=100nF package="100 mil [THT, multilayer]"]
  U2 = mystery part, 5 pins [chip_label=HDC1000]
  S1 = Pushbutton [package="[THT]"]
  S2 = Toggle Switch [package=THT]
  C2 = Electrolytic Capacitor [capacitance=1µF package="100 mil [THT, electrolytic]"]
  U3 = atmega328 [package=dip]
  C3 = Electrolytic Capacitor [capacitance=1µF package="100 mil [THT, electrolytic]"]

nets:
  N1: U1.pin1, C1.0, U2.pin1, C2.+, U3.VCC, C3.+
  N2: U1.pin2, C1.1, U2.pin5, S1.Pin_1, S1.Pin_2, S2.L2, C2.-, U3.GND#7, C3.-
  N3: U1.pin3, U3.D12
  N4: U1.pin4, U3.D11_(PWM)
  N5: U1.pin5, U3.D10_(PWM)
  N6: U1.pin6, U3.D9_(PWM)
  N7: U1.pin7, U3.D8
  N8: U1.pin8, U3.D7
  N9: U2.pin2, U3.A4
  N10: U2.pin3, U3.A5
  N11: U2.pin4, U3.A3
  N12: S1.Pin_3, S1.Pin_4, U3.D2
  N13: S2.COM, U3.D3_(PWM)

notes:
  GND
  +3.3V
  Tact SW
  Wakeup
  Momentary SW
  Sleep/Continuous
  Nokia5110
  1 VCC
  2GND
  3 SCE
  4 RES
  5 D/C
  6 SDIN
  7 SCLK
  8 LED
