# Fritzing sketch HDC1000_LCD5110_ArduinoProMini3.3V_Thermo_1Board  (saved by Fritzing 0.9.3b)
breadboards: 1

parts:
  U1 = mystery part, 8 pins [chip_label=Nokia5110]
  U2 = mystery part, 5 pins [chip_label=HDC1000]
  S1 = Pushbutton [package="[THT]"]
  S2 = Toggle Switch [package=THT]
  C2 = Electrolytic Capacitor [capacitance=1µF package="100 mil [THT, electrolytic]"]
  パーツ1 = Arduino Pro Mini (3.3V)
  U3 = mystery part, 24 pins [chip_label="FT232 Kit"]
  R1 = Resistor [tolerance=±5% resistance=1k package=THT]
  R2 = Resistor [tolerance=±5% resistance=1k package=THT]
  LED1 = LED - 5mm [color="Red (633nm)" package="5 mm [THT]"]
  LED2 = LED - 5mm [color="Green (570nm)" package="5 mm [THT]"]
  VCC1 = 4 x AAA Battery Mount

nets:
  N1: U1.pin1, U2.pin1, C2.+, U3.pin4, LED1.anode, LED2.anode
  N2: U1.pin2, U2.pin5, S1.Pin_1, S1.Pin_2, S2.L2, C2.-, パーツ1.GND, U3.pin7, VCC1.-
  N3: U2.pin2, パーツ1.A4
  N4: U2.pin3, パーツ1.A5
  N5: S1.Pin_3, S1.Pin_4
  N6: パーツ1.TXO, U3.pin5
  N7: パーツ1.RXI, U3.pin1
  N8: U3.pin22, R2.Pin_1
  N9: U3.pin23, R1.Pin_1
  N10: R1.Pin_0, LED2.cathode
  N11: R2.Pin_0, LED1.cathode

notes:
  GND
  +3.3V
  Tact SW
  Wakeup
  Momentary SW
  Sleep/Continuous
  Nokia5110
  1 VCC
  2GND
  3 SCE
  4 RES
  5 D/C
  6 SDIN
  7 SCLK
  8 LED
  HDC1000
  1 +V
  2 SDA
  3 SCL
  4 RDY
  5 GND
  FT232RL Module
  1 TXD 24 GND
  2 DTR# 23 CB0(TXLED#)
  3 RTS# 22 CB1(RXLED#)
  4 VIO 21 VCC
  5 RXD 20 RESET#
  6 RI# 19 3V3
  7 GND 18 CB3
  8 DSR# 17 PU1
  9 DCD# 16 PU2
  10 CTS# 15 VCC
  11 CB4 14 USB
  12 CB2 13 SLD
  FT232RL Module JP
  JP1 2-3 short (VIO=3.3V)
  JP2 1-2 short (USB Power)
